# Fritzing sketch nRF24L02 (saved by Fritzing 0.3.16b)
breadboards: 1

parts:
  Arduino1 = Arduino
  R1 = Resistor [resistance=10k package=THT]
  R2 = Resistor [resistance=10k package=THT]
  R3 = Resistor [resistance=10k package=THT]
  R4 = Resistor [resistance=10k package=THT]
  R5 = Resistor [resistance=15k package=THT]
  R6 = Resistor [resistance=15k package=THT]
  R7 = Resistor [resistance=15k package=THT]
  R8 = Resistor [resistance=15k package=THT]
  IC1 = IC, DIP package, 8 pins [chip_label=nRF24L01 spacing=300mil]

nets:
  N1: Arduino1.GND, R5.Pin_1, R6.Pin_1, R7.Pin_1, R8.Pin_1, IC1.pin1
  N2: Arduino1.D13, IC1.pin5
  N3: Arduino1.D12, IC1.pin4
  N4: Arduino1.D11, R1.Pin_0
  N5: Arduino1.D10, R2.Pin_0
  N6: Arduino1.D9, R3.Pin_0
  N7: Arduino1.D8, R4.Pin_0
  N8: Arduino1.3V3, IC1.pin8
  N9: R1.Pin_1, R5.Pin_0, IC1.pin6
  N10: R2.Pin_1, R6.Pin_0, IC1.pin3
  N11: R3.Pin_1, R7.Pin_0, IC1.pin7
  N12: R4.Pin_1, R8.Pin_0, IC1.pin2
