# Fritzing sketch sensor (saved by Fritzing 0.8.3b)
circuit board: 16.9333cm x 5.64444cm
breadboards: 1

parts:
  Part1 = Arduino Uno (Rev3)
  PIR1 = PIR sensor
  IC2 = IC, DIP package, 8 pins [chip_label=nRF24L01 spacing=300mil]

nets:
  N1: Part1.ICSP_SCK, Part1.D13/SCK, IC2.pin5
  GND: Part1.GND, PIR1.GND, IC2.pin1
  N2: Part1.D9_PWM, IC2.pin3
  N3: Part1.D10_PWM/SS, IC2.pin4
  N4: Part1.D11_PWM/MOSI, IC2.pin6
  N5: Part1.D12/MISO, IC2.pin7
  N6: Part1.D3_PWM, PIR1.SIG
  N7: Part1.3V3, IC2.pin2
  5V: Part1.5V, PIR1.VDD
