# Fritzing sketch server (saved by Fritzing 0.8.3b)
breadboards: 1

parts:
  IC3 = IC, DIP package, 8 pins [chip_label=nRF24L01 spacing=300mil]
  Raspberry_Pi_rev1 = Raspberry Pi rev2

nets:
  N1: IC3.pin1, Raspberry_Pi_rev1.GND
  N2: IC3.pin2, Raspberry_Pi_rev1.3V3
  N3: IC3.pin3, Raspberry_Pi_rev1.GPIO_25
  N4: IC3.pin4, Raspberry_Pi_rev1.GPIO_24
  N5: IC3.pin5, Raspberry_Pi_rev1.GPIO_11
  N6: IC3.pin6, Raspberry_Pi_rev1.GPIO_10
  N7: IC3.pin7, Raspberry_Pi_rev1.GPIO_9
